# Fritzing sketch NiteLite (saved by Fritzing 0.7.12b)
breadboards: 1

parts:
  LED1 = RGB LED - (4 legs) [package="5 mm [THT]"]
  PCB1 = Arduino Shield PCB [sticky=true]  # not connected
  Night_Light_Shield = Arduino
  J1 = screw terminal, 4 pins
  +12V_DC_Centre_+ = Power plug
  RESET = Pushbutton [package="[THT]"]
  ULN2003A = ULN2003A [package="DIP16 [THT]"]
  S2 = Pushbutton [package="[THT]"]
  S3 = Pushbutton [package="[THT]"]
  R6 = Resistor [tolerance=±5% resistance=10k package=THT]
  R7 = Resistor [tolerance=±5% resistance=10k package=THT]
  J3 = Screw terminal - 2 pins [part_number=OFFBTN package=THT]
  R8 = Photocell (LDR) [part_number=LDR package=THT]
  R9 = Resistor [tolerance=±5% resistance=100k package=THT]
  J2 = screw terminal, 4 pins
  J4 = Screw terminal - 2 pins [part_number=LDR package=THT]
  R10 = Resistor [tolerance=±5% resistance=100k package=THT]
  D13 = smd LED [color="Red (633nm)" package="0805 [SMD]"]
  R5 = Resistor [tolerance=±5% resistance=220 package="0805 [SMD]"]
  R1 = Resistor [tolerance=±5% resistance=180 package="0805 [SMD]"]
  R2 = Resistor [tolerance=±5% resistance=100 package="0805 [SMD]"]
  R3 = Resistor [tolerance=±5% resistance=100 package="0805 [SMD]"]
  J5 = male pin header, 2 pins [form="♂ (male)"]
  R4 = Resistor [tolerance=±5% resistance=220 package="0805 [SMD]"]
  PWR = smd LED [color="Red (633nm)" package="0805 [SMD]"]

nets:
  N1: LED1.red_cathode, R1.Pin_1
  N2: LED1.common_anode, J5.pin2
  N3: LED1.green_cathode, R2.Pin_1
  N4: LED1.blue_cathode, R3.Pin_1
  GND: Night_Light_Shield.GND, +12V_DC_Centre_+.GND, RESET.Pin_1, RESET.Pin_2, ULN2003A.0V, S2.Pin_1, S2.Pin_2, S3.Pin_1, S3.Pin_2, J3.pin1, R9.Pin_1, J2.pin2, J2.pin3, R10.Pin_1, D13.cathode, PWR.cathode
  N5: Night_Light_Shield.D13, R5.Pin_1
  N6: Night_Light_Shield.D12, S2.Pin_3, S2.Pin_4, R7.Pin_0, J2.pin4
  N7: Night_Light_Shield.D11, R3.Pin_0
  N8: Night_Light_Shield.D10, R2.Pin_0
  N9: Night_Light_Shield.D9, R1.Pin_0
  N10: Night_Light_Shield.D6, ULN2003A.In_3
  N11: Night_Light_Shield.D5, ULN2003A.In_2
  N12: Night_Light_Shield.D3, ULN2003A.In_1
  N13: Night_Light_Shield.D2, S3.Pin_3, S3.Pin_4, R6.Pin_0, J3.pin2
  N14: Night_Light_Shield.RST, RESET.Pin_3, RESET.Pin_4
  5V: Night_Light_Shield.+5V, R6.Pin_1, R7.Pin_1, R8.pin_0, J4.pin2, J5.pin1, R4.Pin_1
  12V: Night_Light_Shield.VIN, J1.pin4, +12V_DC_Centre_+.VCC, J2.pin1
  N15: Night_Light_Shield.A1, R8.pin_1, R9.Pin_0
  N16: Night_Light_Shield.A2, J4.pin1, R10.Pin_0
  N17: J1.pin1, ULN2003A.Out_3
  N18: J1.pin2, ULN2003A.Out_2
  N19: J1.pin3, ULN2003A.Out_1
  N20: D13.anode, R5.Pin_0
  N21: R4.Pin_0, PWR.anode

notes:
  Motion Activated RGB Strip Night Light, 1.3
  12VDC
  Centre +VE
  R
  +
  G
  B
  +12   -
  PIR
  Night Light
  2012 - JH
  CC BY-NC-SA
  Rev. 1.5
  External LDR Input

custom parts:
  Arduino Shield PCB: Plain PCB Shaped to fit an Arduino "Shield"
